// Logisim project fpa.circ as structural Verilog: 5 circuits, main circuit main
module main (
  input  [15:0] in_1,
  input  [15:0] in_2,
  output [3:0] out_3,
  output Sign,
  output [3:0] Exponent,
  output [13:0] out_6,
  output [10:0] Fraction,
  output [13:0] out_8,
  output [3:0] out_9,
  output [13:0] out_10,
  output [13:0] out_11
);

  wire normalize_1_direction, not_1_out, small_alu_1_flag;
  wire [3:0] adder_2_out, normalize_1_amount, subtractor_1_out;
  wire [12:0] normalize_1_bits_13, shifter_2_out, shifter_3_out;
  wire [12:11] multiplexer_5_out;
  wire [13:0] fractionextender_1_extendedfraction, fractionextender_2_extendedfraction, n2scom_1_out_2;

  FractionExtender fractionextender_1 (
    .ExtendedFraction(fractionextender_1_extendedfraction), .Sign(in_1[15]), .Fraction(in_1[10:0]));
  Small_ALU small_alu_1 (.Difference(out_9), .Flag(small_alu_1_flag), .E1(in_1[14:11]), .E2(in_2[14:11]));
  FractionExtender fractionextender_2 (
    .ExtendedFraction(fractionextender_2_extendedfraction), .Sign(in_2[15]), .Fraction(in_2[10:0]));
  not not_1 (not_1_out, small_alu_1_flag);
  Multiplexer #(.width(14), .enable("false")) multiplexer_1 (
    .in0(fractionextender_1_extendedfraction), .in1(fractionextender_2_extendedfraction), .out(out_6),
    .sel(small_alu_1_flag));
  Multiplexer #(.width(14), .enable("false")) multiplexer_2 (
    .in0(fractionextender_1_extendedfraction), .in1(fractionextender_2_extendedfraction), .out(out_11),
    .sel(not_1_out));
  Multiplexer #(.width(4), .enable("false")) multiplexer_3 (
    .in0(in_1[14:11]), .in1(in_2[14:11]), .out(out_3), .sel(small_alu_1_flag));
  Shifter #(.width(14), .shift("ar")) shifter_1 (.in(out_11), .\dist (out_9), .out(out_10));
  Adder #(.width(14)) adder_1 (.a(out_6), .b(out_10), .out(out_8));  // open: cin, cout
  _2sCom u_2scom_1 (.in_1(out_8), .out_2(n2scom_1_out_2));
  Normalize normalize_1 (
    .Input_14(n2scom_1_out_2), .Direction(normalize_1_direction), .Amount(normalize_1_amount),
    .Bits_13(normalize_1_bits_13));
  Subtractor #(.width(4)) subtractor_1 (.a(out_3), .b(normalize_1_amount), .out(subtractor_1_out));  // open: bin, bout
  Adder #(.width(4)) adder_2 (.a(out_3), .b(normalize_1_amount), .out(adder_2_out));  // open: cin, cout
  Shifter #(.width(13)) shifter_2 (.in(normalize_1_bits_13), .\dist (normalize_1_amount), .out(shifter_2_out));
  Shifter #(.width(13), .shift("lr")) shifter_3 (
    .in(normalize_1_bits_13), .\dist (normalize_1_amount), .out(shifter_3_out));
  Multiplexer #(.width(4), .enable("false")) multiplexer_4 (
    .in0(subtractor_1_out), .in1(adder_2_out), .out(Exponent), .sel(normalize_1_direction));
  Multiplexer #(.width(13), .enable("false")) multiplexer_5 (
    .in0(shifter_2_out), .in1(shifter_3_out), .out({multiplexer_5_out, Fraction}), .sel(normalize_1_direction));

  assign Sign = out_8[13];
endmodule

module Small_ALU (
  input  [3:0] E1,
  input  [3:0] E2,
  output [3:0] Difference,
  output Flag
);

  wire [3:0] negator_1_out, subtractor_1_out;

  Subtractor #(.width(4)) subtractor_1 (.a(E1), .b(E2), .out(subtractor_1_out), .bout(Flag));  // open: bin
  Negator #(.width(4)) negator_1 (.in(subtractor_1_out), .out(negator_1_out));
  Multiplexer #(.width(4), .enable("false")) multiplexer_1 (
    .in0(subtractor_1_out), .in1(negator_1_out), .out(Difference), .sel(Flag));

  // Notes on the sheet:
  //   Flag = 1 when E1 < E2 and Flag = 0 when E1 >= E2
endmodule

module FractionExtender (
  input  Sign,
  input  [10:0] Fraction,
  output [13:0] ExtendedFraction
);

  wire [11:0] bit_extender_1_out;
  wire [12:0] bit_extender_2_out, multiplexer_1_out, negator_1_out;

  assign bit_extender_1_out = {{1{1'b1}}, Fraction};  // Bit_Extender bit_extender_1
  assign bit_extender_2_out = {{1{1'b0}}, bit_extender_1_out};  // Bit_Extender bit_extender_2
  Negator #(.width(13)) negator_1 (.in(bit_extender_2_out), .out(negator_1_out));
  Multiplexer #(.width(13), .enable("false")) multiplexer_1 (
    .in0(bit_extender_2_out), .in1(negator_1_out), .out(multiplexer_1_out), .sel(Sign));
  assign ExtendedFraction = {{1{Sign}}, multiplexer_1_out};  // Bit_Extender bit_extender_3
endmodule

module Normalize (
  input  [13:0] Input_14,
  output [3:0] Amount,
  output Direction,
  output [12:0] Bits_13
);

  wire [3:0] priority_encoder_1_out, subtractor_1_out;

  Priority_Encoder #(.select(4)) priority_encoder_1 (
    .in0(Input_14[0]), .in1(Input_14[1]), .in2(Input_14[2]), .in3(Input_14[3]), .in4(Input_14[4]),
    .in5(Input_14[5]), .in6(Input_14[6]), .in7(Input_14[7]), .in8(Input_14[8]), .in9(Input_14[9]),
    .in10(Input_14[10]), .out(priority_encoder_1_out));  // open: in11, in12, in13, in14, in15, gs, en_out, en_in
  Subtractor #(.width(4)) subtractor_1 (
    .a(4'b1011), .b(priority_encoder_1_out), .out(subtractor_1_out));  // open: bin, bout
  Multiplexer #(.select(2), .width(4), .enable("false")) multiplexer_1 (
    .in0(subtractor_1_out), .in1(4'b0000), .in2(4'b0001), .in3(4'b0001), .out(Amount), .sel(Input_14[12:11]));

  assign Bits_13 = Input_14[12:0];
  assign Direction = Input_14[12];

  // Notes on the sheet:
  //   Flag 0 = Left  Flag = 1 Right
endmodule

module _2sCom (
  input  [13:0] in_1,
  output [13:0] out_2
);

  wire [12:0] multiplexer_1_out, negator_1_out;

  Negator #(.width(13)) negator_1 (.in(in_1[12:0]), .out(negator_1_out));
  Multiplexer #(.width(13), .enable("false")) multiplexer_1 (
    .in0(in_1[12:0]), .in1(negator_1_out), .out(multiplexer_1_out), .sel(in_1[13]));
  assign out_2 = {{1{in_1[13]}}, multiplexer_1_out};  // Bit_Extender bit_extender_1
endmodule
