// Logisim project roundinghardware.circ as structural Verilog: 1 circuit, main circuit main
module main (
  input  [15:0] Adder_result
);

  wire and_1_out, decoder_1_out0, decoder_1_out1, decoder_1_out2, decoder_1_out3, decoder_1_out4,
       decoder_1_out5, decoder_1_out6, decoder_1_out7, not_1_out, or_1_out, or_2_out, or_3_out;

  Decoder #(.select(3), .enable("false")) decoder_1 (
    .out0(decoder_1_out0), .out1(decoder_1_out1), .out2(decoder_1_out2), .out3(decoder_1_out3),
    .out4(decoder_1_out4), .out5(decoder_1_out5), .out6(decoder_1_out6), .out7(decoder_1_out7),
    .sel(Adder_result[13:11]));
  or or_1 (or_1_out, decoder_1_out0, decoder_1_out1, decoder_1_out2, decoder_1_out3);
  or or_2 (or_2_out, decoder_1_out7, decoder_1_out6, decoder_1_out5);
  and and_1 (and_1_out, Adder_result[10], decoder_1_out4);
  not not_1 (not_1_out, or_1_out);
  or or_3 (or_3_out, not_1_out, and_1_out, or_2_out);

  // Notes on the sheet:
  //   1
endmodule
